// Logisim project InputHandler.circ as structural Verilog: 4 circuits, main circuit 22T32
module _22T32 (
  input  [21:0] _22bit_input,
  output [31:0] _32bit_output
);


  assign _32bit_output = {2'b01, _22bit_input, {8{1'b0}}};
endmodule

// IPc
module Input_Processor (
  input  [31:0] A,
  output Sign,
  output [31:0] _32_bit_significand,
  output [8:0] _9_bit_exponent
);

  _22T32 u_22t32_1 (._22bit_input(A[21:0]), ._32bit_output(_32_bit_significand));

  assign _9_bit_exponent = A[30:22];
  assign Sign = A[31];
endmodule

// EDF
module Exponent_Differentiator (
  input  [8:0] Ea,
  input  [8:0] Eb,
  input  Sa,
  input  Sb,
  output Ea___Eb,
  output [8:0] Ea_nEb,
  output [8:0] Larger_Exponent,
  output Larger_s_sign,
  output Smaller_s_sign
);

  wire [8:0] multiplexer_1_out;
  wire [9:9] subtractor_1_out;

  Comparator #(.width(9), .mode("unsigned")) comparator_1 (.a(Ea), .b(Eb), .gt(Ea___Eb));  // open: eq, lt
  Multiplexer #(.width(9)) multiplexer_1 (.in0(Ea), .in1(Eb), .out(multiplexer_1_out), .sel(Ea___Eb), .en(1'b1));
  Multiplexer #(.width(9)) multiplexer_2 (.in0(Eb), .in1(Ea), .out(Larger_Exponent), .sel(Ea___Eb), .en(1'b1));
  Multiplexer multiplexer_3 (.in0(Sb), .in1(Sa), .out(Larger_s_sign), .sel(Ea___Eb), .en(1'b1));
  Multiplexer multiplexer_4 (.in0(Sa), .in1(Sb), .out(Smaller_s_sign), .sel(Ea___Eb), .en(1'b1));
  Subtractor #(.width(10)) subtractor_1 (
    .a({1'b0, Larger_Exponent}), .b({1'b0, multiplexer_1_out}), .out({subtractor_1_out[9], Ea_nEb}));  // open: bin, bout
endmodule

// IpH
module Input (
  input  [31:0] A,
  input  [31:0] B,
  output Larger_s_Sign,
  output [31:0] Larger_s_Fraction,
  output [31:0] Shifted_Smaller_s_Fraction,
  output [31:0] Smaller_s_Fraction,
  output [8:0] Larger_Exponent,
  output [8:0] Exponent_Difference,
  output Smaller_s_sign
);

  wire exponent_differentiator_1_ea___eb, input_processor_1_sign, input_processor_2_sign;
  wire [8:0] input_processor_1__9_bit_exponent, input_processor_2__9_bit_exponent;
  wire [31:0] input_processor_1__32_bit_significand, input_processor_2__32_bit_significand;

  Input_Processor input_processor_1 (
    .A(A), .Sign(input_processor_1_sign), ._32_bit_significand(input_processor_1__32_bit_significand),
    ._9_bit_exponent(input_processor_1__9_bit_exponent));
  Input_Processor input_processor_2 (
    .A(B), .Sign(input_processor_2_sign), ._32_bit_significand(input_processor_2__32_bit_significand),
    ._9_bit_exponent(input_processor_2__9_bit_exponent));
  Exponent_Differentiator exponent_differentiator_1 (
    .Ea(input_processor_1__9_bit_exponent), .Eb(input_processor_2__9_bit_exponent),
    .Sa(input_processor_1_sign), .Sb(input_processor_2_sign), .Larger_Exponent(Larger_Exponent),
    .Ea___Eb(exponent_differentiator_1_ea___eb), .Ea_nEb(Exponent_Difference), .Larger_s_sign(Larger_s_Sign),
    .Smaller_s_sign(Smaller_s_sign));
  Multiplexer #(.width(32)) multiplexer_1 (
    .in0(input_processor_2__32_bit_significand), .in1(input_processor_1__32_bit_significand),
    .out(Larger_s_Fraction), .sel(exponent_differentiator_1_ea___eb), .en(1'b1));
  Multiplexer #(.width(32)) multiplexer_2 (
    .in0(input_processor_1__32_bit_significand), .in1(input_processor_2__32_bit_significand),
    .out(Smaller_s_Fraction), .sel(exponent_differentiator_1_ea___eb), .en(1'b1));
  rightShifter rightshifter_1 (
    .Significand(Smaller_s_Fraction), .Exponent_Difference(Exponent_Difference),
    .Output(Shifted_Smaller_s_Fraction));
endmodule
